# Fritzing sketch soundcard-interface (saved by Fritzing 0.9.6b)
breadboards: 1

parts:
  U1 = Sharp PC847X [package=THT]
  LED1 = LED - 5mm [color="Red (633nm)" current=0.030 package="5 mm [THT]"]
  LED2 = smd LED [color="Blue (430nm)" package="1206 [SMD]"]
  R1 = Resistor [tolerance=±5% power=0.25 resistance=220 package=THT]
  R2 = Resistor [tolerance=±5% power=0.25 resistance=220 package=THT]
  R3 = Resistor [tolerance=±5% power=0.25 resistance=220 package=THT]
  R4 = Resistor [tolerance=±5% power=0.25 resistance=100k package=THT]
  R5 = Resistor [tolerance=±5% power=0.25 resistance=100k package=THT]
  C1 = Ceramic Capacitor [capacitance=100nF voltage=6.3V package="100 mil [THT, multilayer]"]
  R6 = Trimmer Potentiometer [maximum_resistance=10kΩ package=THT]
  R7 = Resistor [tolerance=±5% power=0.25 resistance=1k package=THT]
  J4 = female pin header, 3 pins [form="♀ (female)"]
  J3 = female pin header, 3 pins [form="♀ (female)"]
  J2 = female pin header, 4 pins [form="♀ (female)"]
  R8 = Resistor [tolerance=±5% power=0.25 resistance=1k package=THT]

nets:
  N1: U1.Pin_1, R3.Pin_1
  N2: U1.Pin_15, J3.pin1, J2.pin3
  N3: U1.Pin_16, J2.pin2
  N4: LED1.anode, R1.Pin_1
  N5: LED2.anode, R2.Pin_1
  N6: R2.Pin_0, J4.pin2
  N7: R3.Pin_0, J4.pin3
  N8: R4.Pin_0, R5.Pin_0, C1.1
  N9: R4.Pin_1, R5.Pin_1, J2.pin4
  N10: C1.0, J3.pin3
  GND: R6.leg1, R7.Pin_1, J4.pin1
  N11: R6.wiper, R8.Pin_0
  N12: R6.leg2, R7.Pin_0, J3.pin2
  N13: J2.pin1, R8.Pin_1

notes:
  GPIO 13
  GPIO 4
  Gnd
  PTT
  Mic+
  Spkr+
  Mic
  Left
